// Logisim project MIPS_Claudio_New.circ as structural Verilog: 11 circuits, main circuit somador1bit
module MIPS (
  input  CLK_Manual,
  input  in_2,
  input  ControlCLK
);

  wire ALUOP0, ALUOP1, ALUOP2, ALUsrc, and_1_out, Branch, CLK, CLK_Automatico_out, Halt, Jump, MemRead,
       MemtoReg, MemWrite, multiplexer_1_out, not_1_out, not_2_out, RegDst, RegWrite, ula16bits_1_zero;
  wire [2:0] controlleralu_1_saida, multiplexer_2_out, rom_1_data_2, rom_1_data_3;
  wire [5:0] bit_extender_1_out, bit_extender_2_out, multiplexer_4_out, multiplexer_5_out, pc_1_out_5,
       rom_1_data_4, somador6bits_1_saida, somador6bits_2_saida;
  wire [15:0] bit_extender_3_out, multiplexer_3_out, multiplexer_6_out, ram_1_dout,
       registrador_8x16_sistema_1_sr1, registrador_8x16_sistema_1_sr2, ula16bits_1_saida;
  wire [15:12] rom_1_data;

  Clock CLK_Automatico (.out(CLK_Automatico_out));
  not not_1 (not_1_out, CLK_Manual);
  Multiplexer multiplexer_1 (.in0(not_1_out), .in1(CLK_Automatico_out), .out(multiplexer_1_out), .sel(ControlCLK));
  assign CLK = not_2_out ? multiplexer_1_out : 1'bz;  // Controlled_Buffer controlled_buffer_1
  not not_2 (not_2_out, Halt);
  PC pc_1 (.PC_On(1'b1), .A(multiplexer_5_out), .CLK(CLK), .CLR(in_2), .out_5(pc_1_out_5));
  ROM #(.addrWidth(6), .dataWidth(16)) rom_1 (
    .addr(pc_1_out_5), .data({rom_1_data, rom_1_data_3, rom_1_data_2, rom_1_data_4}));
  somador6bits somador6bits_1 (.A(6'b000001), .B(pc_1_out_5), .Saida(somador6bits_1_saida));
  Bit_Extender #(.in_width(16), .out_width(6), .\type ("zero")) bit_extender_1 (
    .in({rom_1_data, rom_1_data_3, rom_1_data_2, rom_1_data_4}), .out(bit_extender_1_out));
  Bit_Extender #(.in_width(16), .out_width(6), .\type ("zero")) bit_extender_2 (
    .in(bit_extender_3_out), .out(bit_extender_2_out));
  somador6bits somador6bits_2 (.A(somador6bits_1_saida), .B(bit_extender_2_out), .Saida(somador6bits_2_saida));
  Multiplexer #(.width(3)) multiplexer_2 (
    .in0(rom_1_data_2), .in1(rom_1_data_4[5:3]), .out(multiplexer_2_out), .sel(RegDst));
  Controller controller_1 (
    .Opcode(rom_1_data), .RegDst(RegDst), .ALUscr(ALUsrc), .MemToReg(MemtoReg), .RegWrite(RegWrite),
    .Branch(Branch), .ALUOp2(ALUOP2), .ALUOp1(ALUOP1), .ALUOp0(ALUOP0), .Jump(Jump), .MemWrite(MemWrite),
    .MemRead(MemRead), .Halt(Halt));
  Registrador_8x16_Sistema registrador_8x16_sistema_1 (
    .Rdata2(rom_1_data_2), .Write(RegWrite), .Reset(in_2), .CLK(CLK), .Rdata1(rom_1_data_3),
    .Wreg(multiplexer_2_out), .Entrada(multiplexer_6_out), .Sr1(registrador_8x16_sistema_1_sr1),
    .Sr2(registrador_8x16_sistema_1_sr2));
  Multiplexer #(.width(16)) multiplexer_3 (
    .in0(registrador_8x16_sistema_1_sr2), .in1(bit_extender_3_out), .out(multiplexer_3_out), .sel(ALUsrc));
  assign bit_extender_3_out = {{10{rom_1_data_4[5]}}, rom_1_data_4};  // Bit_Extender bit_extender_3
  Multiplexer #(.width(6)) multiplexer_4 (
    .in0(somador6bits_1_saida), .in1(somador6bits_2_saida), .out(multiplexer_4_out), .sel(and_1_out));
  and and_1 (and_1_out, Branch, ula16bits_1_zero);
  Multiplexer #(.width(6)) multiplexer_5 (
    .in0(multiplexer_4_out), .in1(bit_extender_1_out), .out(multiplexer_5_out), .sel(Jump));
  ULA16bits ula16bits_1 (
    .A(registrador_8x16_sistema_1_sr1), .B(multiplexer_3_out), .Seletor(controlleralu_1_saida),
    .Zero(ula16bits_1_zero), .Saida(ula16bits_1_saida));
  ControllerALU controlleralu_1 (
    .OpALU({ALUOP2, ALUOP1, ALUOP0}), .Funct(rom_1_data_4[2:0]), .Saida(controlleralu_1_saida));
  RAM #(.addrWidth(16), .dataWidth(16), .trigger("falling")) ram_1 (
    .addr(ula16bits_1_saida), .we(MemWrite), .oe(MemRead), .clk(CLK), .din(registrador_8x16_sistema_1_sr2),
    .dout(ram_1_dout));
  Multiplexer #(.width(16)) multiplexer_6 (
    .in0(ula16bits_1_saida), .in1(ram_1_dout), .out(multiplexer_6_out), .sel(MemtoReg));

  // Other names for the same wires on the sheet: CLR = in_2
endmodule

module somador1bit (
  input  A,
  input  B,
  input  Cin,
  output S,
  output Count
);

  wire and_1_out, and_2_out, and_3_out, and_4_out, and_5_out, and_6_out, and_7_out, not_1_out, not_2_out,
       not_3_out;

  not not_1 (not_1_out, Cin);
  not not_2 (not_2_out, B);
  not not_3 (not_3_out, A);
  and and_1 (and_1_out, A, B, Cin);
  and and_2 (and_2_out, not_1_out, A, not_2_out);
  and and_3 (and_3_out, not_1_out, B, not_3_out);
  and and_4 (and_4_out, Cin, not_2_out, not_3_out);
  and and_5 (and_5_out, Cin, B);
  and and_6 (and_6_out, A, Cin);
  and and_7 (and_7_out, B, A);
  or or_1 (S, and_1_out, and_2_out, and_3_out, and_4_out);
  or or_2 (Count, and_5_out, and_6_out, and_7_out);
endmodule

module ULA16bits (
  input  [15:0] A,
  input  [15:0] B,
  input  [2:0] Seletor,
  output Zero,
  output [15:0] Saida
);

  wire somador16bits_1_out_5;
  wire [15:0] and_1_out, multiplexer_1_out, nand_1_out, nor_2_out, or_1_out, somador16bits_1_out_4,
       xor_1_out, xor_2_out;
  wire [15:15] or_2_out;

  nor nor_1 (Zero, Saida[0], Saida[1], Saida[2], Saida[3], Saida[4], Saida[5], Saida[6], Saida[7], Saida[8], Saida[9], Saida[10], Saida[11], Saida[12], Saida[13], Saida[14], Saida[15]);
  assign and_1_out = A & B;  // AND_Gate and_1, 16 bits wide
  assign or_1_out = A | B;  // OR_Gate or_1, 16 bits wide
  assign nand_1_out = ~(A & B);  // NAND_Gate nand_1, 16 bits wide
  assign nor_2_out = ~(A | B);  // NOR_Gate nor_2, 16 bits wide
  assign xor_1_out = B ^ {16{or_2_out[15]}};  // XOR_Gate xor_1, 16 bits wide
  assign xor_2_out = A ^ B;  // XOR_Gate xor_2, 16 bits wide
  Multiplexer #(.width(16)) multiplexer_1 (
    .in0(16'h1), .in1({16{1'b0}}), .out(multiplexer_1_out), .sel(somador16bits_1_out_5));
  somador16bits somador16bits_1 (
    .in_2(A), .in_3(xor_1_out), .in_1(or_2_out[15]), .out_5(somador16bits_1_out_5),
    .out_4(somador16bits_1_out_4));
  or or_2 (or_2_out[15], Seletor[0], Seletor[1], Seletor[2]);
  Multiplexer #(.select(3), .width(16)) multiplexer_2 (
    .in0(somador16bits_1_out_4), .in1(somador16bits_1_out_4), .in2(and_1_out), .in3(or_1_out),
    .in4(nand_1_out), .in5(nor_2_out), .in6(xor_2_out), .in7(multiplexer_1_out), .out(Saida), .sel(Seletor));

  // Notes on the sheet:
  //   Mnemonico
  //   SOMA
  //   SUB
  //   AND
  //   OUR
  //   NAND
  //   NOUR
  //   XNOR
  //   RESERV
  //   Código
  //   000
  //   001
  //   010
  //   011
  //   100
  //   101
  //   110
  //   111
endmodule

module somador4bits (
  input  in_1,
  input  [3:0] in_2,
  input  [3:0] in_3,
  output [3:0] out_4,
  output out_5
);

  wire somador1bit_1_count, somador1bit_2_count, somador1bit_3_count;

  somador1bit somador1bit_1 (.A(in_2[0]), .B(in_3[0]), .Cin(in_1), .S(out_4[0]), .Count(somador1bit_1_count));
  somador1bit somador1bit_2 (
    .A(in_2[1]), .B(in_3[1]), .Cin(somador1bit_1_count), .S(out_4[1]), .Count(somador1bit_2_count));
  somador1bit somador1bit_3 (
    .A(in_2[2]), .B(in_3[2]), .Cin(somador1bit_2_count), .S(out_4[2]), .Count(somador1bit_3_count));
  somador1bit somador1bit_4 (.A(in_2[3]), .B(in_3[3]), .Cin(somador1bit_3_count), .S(out_4[3]), .Count(out_5));
endmodule

module somador8bits (
  input  Cin,
  input  [7:0] in_2,
  input  [7:0] in_3,
  output [7:0] out_4,
  output out_5
);

  wire somador4bits_1_out_5;

  somador4bits somador4bits_1 (
    .in_2(in_2[3:0]), .in_3(in_3[3:0]), .in_1(Cin), .out_5(somador4bits_1_out_5), .out_4(out_4[3:0]));
  somador4bits somador4bits_2 (
    .in_2(in_2[7:4]), .in_3(in_3[7:4]), .in_1(somador4bits_1_out_5), .out_5(out_5), .out_4(out_4[7:4]));
endmodule

module somador16bits (
  input  in_1,
  input  [15:0] in_2,
  input  [15:0] in_3,
  output [15:0] out_4,
  output out_5
);

  wire somador8bits_1_out_5;

  somador8bits somador8bits_1 (
    .in_2(in_2[7:0]), .in_3(in_3[7:0]), .Cin(in_1), .out_5(somador8bits_1_out_5), .out_4(out_4[7:0]));
  somador8bits somador8bits_2 (
    .in_2(in_2[15:8]), .in_3(in_3[15:8]), .Cin(somador8bits_1_out_5), .out_5(out_5), .out_4(out_4[15:8]));
endmodule

module PC (
  input  [5:0] A,
  input  PC_On,
  input  CLK,
  input  CLR,
  output [5:0] out_5
);

  wire [5:0] controlled_buffer_1_out;

  assign controlled_buffer_1_out = PC_On ? A : 6'bz;  // Controlled_Buffer controlled_buffer_1
  D_Flip_Flop d_ff_1 (.D(controlled_buffer_1_out[0]), .clk(CLK), .Q(out_5[0]), .reset(CLR));  // open: Qn, preset
  D_Flip_Flop d_ff_2 (.D(controlled_buffer_1_out[1]), .clk(CLK), .Q(out_5[1]), .reset(CLR));  // open: Qn, preset
  D_Flip_Flop d_ff_3 (.D(controlled_buffer_1_out[2]), .clk(CLK), .Q(out_5[2]), .reset(CLR));  // open: Qn, preset
  D_Flip_Flop d_ff_4 (.D(controlled_buffer_1_out[3]), .clk(CLK), .Q(out_5[3]), .reset(CLR));  // open: Qn, preset
  D_Flip_Flop d_ff_5 (.D(controlled_buffer_1_out[4]), .clk(CLK), .Q(out_5[4]), .reset(CLR));  // open: Qn, preset
  D_Flip_Flop d_ff_6 (.D(controlled_buffer_1_out[5]), .clk(CLK), .Q(out_5[5]), .reset(CLR));  // open: Qn, preset
endmodule

module somador6bits (
  input  [5:0] A,
  input  [5:0] B,
  output [5:0] Saida
);

  wire somador1bit_1_count, somador1bit_2_count, somador1bit_3_count, somador1bit_4_count,
       somador1bit_5_count;

  somador1bit somador1bit_1 (.A(A[0]), .B(B[0]), .S(Saida[0]), .Count(somador1bit_1_count));  // open: Cin
  somador1bit somador1bit_2 (.A(A[1]), .B(B[1]), .Cin(somador1bit_1_count), .S(Saida[1]), .Count(somador1bit_2_count));
  somador1bit somador1bit_3 (.A(A[2]), .B(B[2]), .Cin(somador1bit_2_count), .S(Saida[2]), .Count(somador1bit_3_count));
  somador1bit somador1bit_4 (.A(A[3]), .B(B[3]), .Cin(somador1bit_3_count), .S(Saida[3]), .Count(somador1bit_4_count));
  somador1bit somador1bit_5 (.A(A[4]), .B(B[4]), .Cin(somador1bit_4_count), .S(Saida[4]), .Count(somador1bit_5_count));
  somador1bit somador1bit_6 (.A(A[5]), .B(B[5]), .Cin(somador1bit_5_count), .S(Saida[5]));  // open: Count
endmodule

module Registrador_8x16_Sistema (
  input  [15:0] Entrada,
  input  Write,
  input  [2:0] Wreg,
  input  [2:0] Rdata1,
  input  Reset,
  input  CLK,
  input  [2:0] Rdata2,
  output [15:0] Sr1,
  output [15:0] Sr2
);

  wire [15:0] register_1_q, register_2_q, register_3_q, register_4_q, register_5_q, register_6_q,
       register_7_q, register_8_q;
  wire [16:0] demultiplexer_1_out0, demultiplexer_1_out1, demultiplexer_1_out2, demultiplexer_1_out3,
       demultiplexer_1_out4, demultiplexer_1_out5, demultiplexer_1_out6, demultiplexer_1_out7;

  Demultiplexer #(.select(3), .width(17)) demultiplexer_1 (
    .out0(demultiplexer_1_out0), .out1(demultiplexer_1_out1), .out2(demultiplexer_1_out2),
    .out3(demultiplexer_1_out3), .out4(demultiplexer_1_out4), .out5(demultiplexer_1_out5),
    .out6(demultiplexer_1_out6), .out7(demultiplexer_1_out7), .in({Write, Entrada}), .sel(Wreg));
  Register #(.width(16)) register_1 (
    .D(demultiplexer_1_out0[15:0]), .en(demultiplexer_1_out0[16]), .clk(CLK), .Q(register_1_q), .clr(Reset));
  Register #(.width(16)) register_2 (
    .D(demultiplexer_1_out1[15:0]), .en(demultiplexer_1_out1[16]), .clk(CLK), .Q(register_2_q), .clr(Reset));
  Register #(.width(16)) register_3 (
    .D(demultiplexer_1_out2[15:0]), .en(demultiplexer_1_out2[16]), .clk(CLK), .Q(register_3_q), .clr(Reset));
  Register #(.width(16)) register_4 (
    .D(demultiplexer_1_out3[15:0]), .en(demultiplexer_1_out3[16]), .clk(CLK), .Q(register_4_q), .clr(Reset));
  Register #(.width(16)) register_5 (
    .D(demultiplexer_1_out4[15:0]), .en(demultiplexer_1_out4[16]), .clk(CLK), .Q(register_5_q), .clr(Reset));
  Register #(.width(16)) register_6 (
    .D(demultiplexer_1_out5[15:0]), .en(demultiplexer_1_out5[16]), .clk(CLK), .Q(register_6_q), .clr(Reset));
  Register #(.width(16)) register_7 (
    .D(demultiplexer_1_out6[15:0]), .en(demultiplexer_1_out6[16]), .clk(CLK), .Q(register_7_q), .clr(Reset));
  Register #(.width(16)) register_8 (
    .D(demultiplexer_1_out7[15:0]), .en(demultiplexer_1_out7[16]), .clk(CLK), .Q(register_8_q), .clr(Reset));
  Multiplexer #(.select(3), .width(16)) multiplexer_1 (
    .in0(register_1_q), .in1(register_2_q), .in2(register_3_q), .in3(register_4_q), .in4(register_5_q),
    .in5(register_6_q), .in6(register_7_q), .in7(register_8_q), .out(Sr1), .sel(Rdata1));
  Multiplexer #(.select(3), .width(16)) multiplexer_2 (
    .in0(register_1_q), .in1(register_2_q), .in2(register_3_q), .in3(register_4_q), .in4(register_5_q),
    .in5(register_6_q), .in6(register_7_q), .in7(register_8_q), .out(Sr2), .sel(Rdata2));
endmodule

module Controller (
  input  [3:0] Opcode,
  output RegDst,
  output ALUscr,
  output MemToReg,
  output RegWrite,
  output Branch,
  output ALUOp2,
  output ALUOp1,
  output ALUOp0,
  output Jump,
  output MemWrite,
  output MemRead,
  output Halt
);

  wire and_2_out, and_3_out, and_5_out, and_6_out, and_7_out, and_8_out, and_10_out, and_11_out, and_12_out,
       and_13_out, and_14_out, and_15_out, and_16_out, and_17_out, and_18_out, and_19_out, and_20_out,
       and_22_out, and_23_out, and_24_out, and_25_out, and_26_out, not_1_out, not_2_out, not_3_out, not_4_out;

  not not_1 (not_1_out, Opcode[3]);
  not not_2 (not_2_out, Opcode[2]);
  not not_3 (not_3_out, Opcode[1]);
  not not_4 (not_4_out, Opcode[0]);
  and and_1 (RegDst, Opcode[2], Opcode[0]);
  and and_2 (and_2_out, not_2_out, Opcode[1]);
  and and_3 (and_3_out, Opcode[3], not_2_out);
  and and_4 (MemToReg, not_2_out, Opcode[1], Opcode[0]);
  and and_5 (and_5_out, not_2_out, Opcode[1]);
  and and_6 (and_6_out, not_1_out, not_4_out);
  and and_7 (and_7_out, Opcode[3], not_2_out);
  and and_8 (and_8_out, Opcode[3], Opcode[1]);
  and and_9 (Branch, Opcode[2], not_3_out, Opcode[0]);
  and and_10 (and_10_out, not_2_out, Opcode[1]);
  and and_11 (and_11_out, not_3_out, not_4_out);
  and and_12 (and_12_out, Opcode[3], Opcode[2], not_3_out);
  and and_13 (and_13_out, not_2_out, Opcode[1], not_4_out);
  and and_14 (and_14_out, Opcode[3], Opcode[2], Opcode[0]);
  and and_15 (and_15_out, Opcode[3], Opcode[1], not_4_out);
  and and_16 (and_16_out, Opcode[1], not_4_out);
  and and_17 (and_17_out, not_1_out, Opcode[2], not_3_out, Opcode[0]);
  and and_18 (and_18_out, Opcode[3], Opcode[2], Opcode[1]);
  and and_19 (and_19_out, not_1_out, Opcode[1], Opcode[0]);
  and and_20 (and_20_out, not_1_out, Opcode[2], Opcode[0]);
  and and_21 (MemWrite, Opcode[2], not_3_out, not_4_out);
  and and_22 (and_22_out, not_2_out, Opcode[0]);
  and and_23 (and_23_out, not_1_out, Opcode[2], Opcode[1]);
  and and_24 (and_24_out, Opcode[3], not_2_out);
  and and_25 (and_25_out, Opcode[3], not_3_out);
  and and_26 (and_26_out, Opcode[1], Opcode[0]);
  and and_27 (Halt, not_1_out, not_2_out, not_3_out, Opcode[0]);
  or or_1 (ALUscr, not_4_out, and_2_out, and_3_out);
  or or_2 (RegWrite, and_5_out, and_6_out, and_7_out, and_8_out);
  or or_3 (ALUOp2, and_10_out, and_11_out, and_12_out);
  or or_4 (ALUOp1, and_13_out, and_14_out, and_15_out);
  or or_5 (ALUOp0, and_16_out, and_17_out, and_18_out);
  or or_6 (Jump, and_19_out, and_20_out);
  or or_7 (MemRead, and_22_out, and_23_out, and_24_out, and_25_out, and_26_out);

  // Notes on the sheet:
  //   ORI: 1010
  //   LW: 1011
  //   SW: 1100
  //   SLTI: 1001
  //   J:0111
  //   R TYPE: 1111
  //   BEQ: 1101
  //   ADDI: 1000
  //   ANDI: 0110
  //   HALT: 0001
endmodule

module ControllerALU (
  input  [2:0] OpALU,
  input  [2:0] Funct,
  output [2:0] Saida
);

  wire and_1_out, and_2_out, and_3_out, and_4_out, and_5_out, and_6_out;

  and and_1 (and_1_out, ~OpALU[0], ~OpALU[1], ~OpALU[2]);  // AND_Gate
  and and_2 (and_2_out, ~OpALU[1], ~OpALU[0], OpALU[2]);  // AND_Gate
  and and_3 (and_3_out, OpALU[1], ~OpALU[2], OpALU[0]);  // AND_Gate
  and and_4 (and_4_out, OpALU[1], OpALU[2], ~OpALU[0]);  // AND_Gate
  and and_5 (and_5_out, OpALU[2], OpALU[1], OpALU[0]);
  and and_6 (and_6_out, ~OpALU[2], ~OpALU[1], OpALU[0]);  // AND_Gate
  assign Saida = and_1_out ? 3'b111 : 3'bz;  // Controlled_Buffer controlled_buffer_1
  assign Saida = and_2_out ? 3'b000 : 3'bz;  // Controlled_Buffer controlled_buffer_2
  assign Saida = and_3_out ? Funct : 3'bz;  // Controlled_Buffer controlled_buffer_3
  assign Saida = and_4_out ? 3'b001 : 3'bz;  // Controlled_Buffer controlled_buffer_4
  assign Saida = and_5_out ? 3'b011 : 3'bz;  // Controlled_Buffer controlled_buffer_5
  assign Saida = and_6_out ? 3'b010 : 3'bz;  // Controlled_Buffer controlled_buffer_6

  // Notes on the sheet:
  //   R-TYPE: 011
  //   ADDI: 100
  //   SUBI: 110
  //   NADA: 000
  //   ORI: 111
  //   ANDI: 001
endmodule
