// Logisim project Sap1_Claudio - Copia.circ as structural Verilog: 6 circuits, main circuit MeioSomador
module MeioSomador (
  input  A,
  input  VEM1,
  output Soma,
  output VAI1
);

  xor xor_1 (Soma, A, VEM1);
  and and_1 (VAI1, VEM1, A);
endmodule

module SomadorCompleto (
  input  A,
  input  B,
  input  Cin,
  output Soma,
  output Vai1
);

  wire and_1_out, and_2_out, xor_1_out;

  xor xor_1 (xor_1_out, A, B);
  and and_1 (and_1_out, A, B);
  xor xor_2 (Soma, xor_1_out, Cin);
  and and_2 (and_2_out, xor_1_out, Cin);
  or or_1 (Vai1, and_2_out, and_1_out);
endmodule

// Complemento1
module Complemento_1 (
  input  A7,
  input  A6,
  input  A5,
  input  A4,
  input  A3,
  input  A2,
  input  A1,
  input  A0,
  input  in_9,
  output R7,
  output R6,
  output R5,
  output R4,
  output R3,
  output R2,
  output R1,
  output R0
);

  xor xor_1 (R7, A7, in_9);
  xor xor_2 (R6, A6, in_9);
  xor xor_3 (R5, A5, in_9);
  xor xor_4 (R4, A4, in_9);
  xor xor_5 (R3, A3, in_9);
  xor xor_6 (R2, A2, in_9);
  xor xor_7 (R1, A1, in_9);
  xor xor_8 (R0, A0, in_9);
endmodule

// Complemento2
module Complemento_2 (
  input  A0,
  input  A1,
  input  A2,
  input  A3,
  input  A4,
  input  A5,
  input  A6,
  input  A7,
  input  in_9,
  output out_10,
  output out_11,
  output out_12,
  output out_13,
  output out_14,
  output out_15,
  output out_16,
  output out_17
);

  wire meiosomador_1_vai1, meiosomador_2_vai1, meiosomador_3_vai1, meiosomador_4_vai1, meiosomador_5_vai1,
       meiosomador_6_vai1, meiosomador_7_vai1;

  MeioSomador meiosomador_1 (.A(A0), .VEM1(in_9), .Soma(out_10), .VAI1(meiosomador_1_vai1));
  MeioSomador meiosomador_2 (.A(A1), .VEM1(meiosomador_1_vai1), .Soma(out_11), .VAI1(meiosomador_2_vai1));
  MeioSomador meiosomador_3 (.A(A2), .VEM1(meiosomador_2_vai1), .Soma(out_12), .VAI1(meiosomador_3_vai1));
  MeioSomador meiosomador_4 (.A(A3), .VEM1(meiosomador_3_vai1), .Soma(out_13), .VAI1(meiosomador_4_vai1));
  MeioSomador meiosomador_5 (.A(A4), .VEM1(meiosomador_4_vai1), .Soma(out_14), .VAI1(meiosomador_5_vai1));
  MeioSomador meiosomador_6 (.A(A5), .VEM1(meiosomador_5_vai1), .Soma(out_15), .VAI1(meiosomador_6_vai1));
  MeioSomador meiosomador_7 (.A(A6), .VEM1(meiosomador_6_vai1), .Soma(out_16), .VAI1(meiosomador_7_vai1));
  MeioSomador meiosomador_8 (.A(A7), .VEM1(meiosomador_7_vai1), .Soma(out_17));  // open: VAI1
endmodule

// SUM/SUB
module Somador_Subtrator (
  input  [7:0] B,
  input  Su,
  input  [7:0] A,
  input  Eu,
  output [7:0] out_5
);

  wire complemento_1_1_r0, complemento_1_1_r1, complemento_1_1_r2, complemento_1_1_r3, complemento_1_1_r4,
       complemento_1_1_r5, complemento_1_1_r6, complemento_1_1_r7, complemento_2_1_out_10,
       complemento_2_1_out_11, complemento_2_1_out_12, complemento_2_1_out_13, complemento_2_1_out_14,
       complemento_2_1_out_15, complemento_2_1_out_16, complemento_2_1_out_17, somador_4bits_1_out_11,
       somador_4bits_1_out_13, somador_4bits_1_out_14, somador_4bits_1_resultado, somador_4bits_1_vai1,
       somador_4bits_2_out_11, somador_4bits_2_out_13, somador_4bits_2_out_14, somador_4bits_2_resultado,
       somador_4bits_2_vai1;

  LED led_1 (.in(somador_4bits_1_vai1));
  Somador_4Bits somador_4bits_1 (
    .Vai1(somador_4bits_1_vai1), .in_1(A[7]), .A(A[6]), .in_3(A[5]), .in_4(A[4]),
    .in_5(complemento_2_1_out_17), .B(complemento_2_1_out_16), .in_7(complemento_2_1_out_15),
    .in_8(complemento_2_1_out_14), .Vem1(somador_4bits_2_vai1), .out_11(somador_4bits_1_out_11),
    .Resultado(somador_4bits_1_resultado), .out_13(somador_4bits_1_out_13), .out_14(somador_4bits_1_out_14));
  assign out_5[5] = Eu ? somador_4bits_1_out_13 : 1'bz;  // Controlled_Buffer controlled_buffer_1
  assign out_5[6] = Eu ? somador_4bits_1_resultado : 1'bz;  // Controlled_Buffer controlled_buffer_2
  assign out_5[7] = Eu ? somador_4bits_1_out_11 : 1'bz;  // Controlled_Buffer controlled_buffer_3
  Somador_4Bits somador_4bits_2 (
    .Vai1(somador_4bits_2_vai1), .in_1(A[3]), .A(A[2]), .in_3(A[1]), .in_4(A[0]),
    .in_5(complemento_2_1_out_13), .B(complemento_2_1_out_12), .in_7(complemento_2_1_out_11),
    .in_8(complemento_2_1_out_10), .Vem1(1'b0), .out_11(somador_4bits_2_out_11),
    .Resultado(somador_4bits_2_resultado), .out_13(somador_4bits_2_out_13), .out_14(somador_4bits_2_out_14));
  assign out_5[1] = Eu ? somador_4bits_2_out_13 : 1'bz;  // Controlled_Buffer controlled_buffer_4
  assign out_5[2] = Eu ? somador_4bits_2_resultado : 1'bz;  // Controlled_Buffer controlled_buffer_5
  assign out_5[3] = Eu ? somador_4bits_2_out_11 : 1'bz;  // Controlled_Buffer controlled_buffer_6
  assign out_5[4] = Eu ? somador_4bits_1_out_14 : 1'bz;  // Controlled_Buffer controlled_buffer_7
  Complemento_2 complemento_2_1 (
    .in_9(Su), .A0(complemento_1_1_r0), .A1(complemento_1_1_r1), .A2(complemento_1_1_r2),
    .A3(complemento_1_1_r3), .A4(complemento_1_1_r4), .A5(complemento_1_1_r5), .A6(complemento_1_1_r6),
    .A7(complemento_1_1_r7), .out_10(complemento_2_1_out_10), .out_11(complemento_2_1_out_11),
    .out_12(complemento_2_1_out_12), .out_13(complemento_2_1_out_13), .out_14(complemento_2_1_out_14),
    .out_15(complemento_2_1_out_15), .out_16(complemento_2_1_out_16), .out_17(complemento_2_1_out_17));
  assign out_5[0] = Eu ? somador_4bits_2_out_14 : 1'bz;  // Controlled_Buffer controlled_buffer_8
  Complemento_1 complemento_1_1 (
    .A7(B[7]), .A6(B[6]), .A5(B[5]), .A4(B[4]), .A3(B[3]), .A2(B[2]), .A1(B[1]), .A0(B[0]),
    .R7(complemento_1_1_r7), .R6(complemento_1_1_r6), .R5(complemento_1_1_r5), .R4(complemento_1_1_r4),
    .R3(complemento_1_1_r3), .R2(complemento_1_1_r2), .R1(complemento_1_1_r1), .R0(complemento_1_1_r0),
    .in_9(Su));
endmodule

// somador 4b
module Somador_4Bits (
  input  in_1,
  input  A,
  input  in_3,
  input  in_4,
  input  in_5,
  input  B,
  input  in_7,
  input  in_8,
  input  Vem1,
  output Vai1,
  output out_11,
  output Resultado,
  output out_13,
  output out_14
);

  wire somadorcompleto_2_vai1, somadorcompleto_3_vai1, somadorcompleto_4_vai1;

  SomadorCompleto somadorcompleto_1 (.A(in_1), .B(in_5), .Cin(somadorcompleto_2_vai1), .Soma(out_11), .Vai1(Vai1));
  SomadorCompleto somadorcompleto_2 (
    .A(A), .B(B), .Cin(somadorcompleto_3_vai1), .Soma(Resultado), .Vai1(somadorcompleto_2_vai1));
  SomadorCompleto somadorcompleto_3 (
    .A(in_3), .B(in_7), .Cin(somadorcompleto_4_vai1), .Soma(out_13), .Vai1(somadorcompleto_3_vai1));
  SomadorCompleto somadorcompleto_4 (.A(in_4), .B(in_8), .Cin(Vem1), .Soma(out_14), .Vai1(somadorcompleto_4_vai1));
endmodule
