// Logisim project Sap1_Claudio.circ as structural Verilog: 14 circuits, main circuit main
module main (
  input  Reset,
  output [7:0] Barramento_8Bits
);

  wire CLK, CLK_out, CLR, Cp, Ea, Ep, Eu, not_1_out, NOT_Ce, NOT_CLK, NOT_CLR, NOT_Ei, NOT_La, NOT_Lb,
       NOT_Li, NOT_Lm, NOT_Lo, ri_1_x4, ri_1_x5, ri_1_x6, ri_1_x7, Su;
  wire [3:0] rem4bits_1_out_4, rs_1_para_display, rs_1_para_display_2;
  wire [5:0] controlador_1_timer;
  wire [7:0] ac_1_para_add_sub, rb_1_para_add_sub, rom_1_data;

  ROM #(.addrWidth(4)) rom_1 (.addr(rem4bits_1_out_4), .data(rom_1_data));
  Clock u_CLK (.out(CLK_out));
  LED T1 (.in(controlador_1_timer[0]));
  LED T2 (.in(controlador_1_timer[1]));
  LED T3 (.in(controlador_1_timer[2]));
  LED T4 (.in(controlador_1_timer[3]));
  LED T5 (.in(controlador_1_timer[4]));
  LED T6 (.in(controlador_1_timer[5]));
  REM4bits rem4bits_1 (.CLK(CLK), .Lm(NOT_Lm), .in_2(Barramento_8Bits[3:0]), .out_4(rem4bits_1_out_4));
  PC pc_1 (.Cp(Cp), .CLK(NOT_CLK), .CLR(NOT_CLR), .Ep(Ep), .Saida(Barramento_8Bits[3:0]));
  RI ri_1 (
    .CLK(CLK), .CLR(CLR), .Ei(NOT_Ei), .Li(NOT_Li), .In(Barramento_8Bits), .X7(ri_1_x7), .X6(ri_1_x6),
    .X5(ri_1_x5), .Out(Barramento_8Bits[3:0]), .X4(ri_1_x4));
  assign Barramento_8Bits = not_1_out ? rom_1_data : 8'bz;  // Controlled_Buffer controlled_buffer_1
  not not_1 (not_1_out, NOT_Ce);
  AC ac_1 (
    .Do_Barramento(Barramento_8Bits), .La(NOT_La), .CLK(CLK), .Ea(Ea), .Para_Barramento(Barramento_8Bits),
    .Para_Add_Sub(ac_1_para_add_sub));
  Hex_Digit_Display hex_digit_display_1 (.value(rs_1_para_display_2));  // open: dp
  Somador_Subtrator somador_subtrator_1 (
    .A(ac_1_para_add_sub), .Eu(Eu), .B(rb_1_para_add_sub), .Su(Su), .out_5(Barramento_8Bits));
  RB rb_1 (.CLK(CLK), .Do_Barramento(Barramento_8Bits), .Lb(NOT_Lb), .Para_Add_Sub(rb_1_para_add_sub));
  RS rs_1 (
    .CLK(CLK), .CLR(CLR), .Do_Barramento(Barramento_8Bits), .La(NOT_Lo),
    .Para_Display({rs_1_para_display_2, rs_1_para_display}));
  Hex_Digit_Display hex_digit_display_2 (.value(rs_1_para_display));  // open: dp
  Controlador controlador_1 (
    .CLR_CPU(Reset), .X7(ri_1_x7), .CLK_CPU(CLK_out), .X6(ri_1_x6), .X5(ri_1_x5), .X4(ri_1_x4), .Ep(Ep),
    .NOT_Lm(NOT_Lm), .NOT_CE(NOT_Ce), .Timer(controlador_1_timer), .NOT_L1(NOT_Li), .NOT_E1(NOT_Ei),
    .NOT_La(NOT_La), .Ea(Ea), .Su(Su), .Eu(Eu), .NOT_Lb(NOT_Lb), .NOT_Lo(NOT_Lo), .NOT_CLR(NOT_CLR),
    .CLR(CLR), .CLK(CLK), .NOT_CLK(NOT_CLK), .Cp(Cp));

  // Notes on the sheet:
  //   LDA 0
  //   ADD 1
  //   SUB 2
  //   OUT e
  //   HLT f
  //   RAM
  //   Memória de acesso aleatório composta
  //   por 16 registradores de 8 bits, usada para
  //   armazenar instruções e dados
  //   e envia o comando correspondente à unidade de controle
  //   Controlador
  //   A unidade de controle coordena as operações do processador
  //   gerenciando as entradas e saídas dos componentes
  //   Contador de Programa
  //   é um registrador que armazena o
  //   endereço da próxima instrução a ser executada
  //   Entrada e REM
  //   é um registrador que está conectado
  //   diretamente com a memoria RAM e aponta
  //   para o endereço que será acessado na memória
  //   Registrador de Instruções
  //   Armazena a instrução recebida, a decodifica
  //   contents of rom_1 (hex, n*v repeats v):
  //   8 29 e0 f0 4*0 8 4
  //   Timer
  //   Acumulador A
  //   É a unidade responsável por realizar operações lógicas e aritméticas.
  //   Registrador B
  //   Funciona como um registrador auxiliar para
  //   armazenar dados usados em operações
  //   Registrador de Saída
  //   Recebe os dados do acumulador e exibe no display.       
  //   O acumulador é um registrador de 8 bits que
  //   armazena o resultado das operações
  //   Somador/Subtrator
endmodule

module MeioSomador (
  input  A,
  input  VEM1,
  output Soma,
  output VAI1
);

  xor xor_1 (Soma, A, VEM1);
  and and_1 (VAI1, VEM1, A);
endmodule

module PC (
  input  Cp,
  input  CLK,
  input  CLR,
  input  Ep,
  output [3:0] Saida
);

  wire j_k_ff_1_qn, j_k_ff_2_qn, j_k_ff_3_qn, not_1_out;
  wire [3:0] j_k_ff_1_q;

  not not_1 (not_1_out, CLR);
  J_K_Flip_Flop j_k_ff_1 (
    .J(Cp), .K(Cp), .clk(CLK), .Q(j_k_ff_1_q[0]), .Qn(j_k_ff_1_qn), .reset(not_1_out));  // open: preset
  J_K_Flip_Flop j_k_ff_2 (
    .J(Cp), .K(Cp), .clk(j_k_ff_1_qn), .Q(j_k_ff_1_q[1]), .Qn(j_k_ff_2_qn), .reset(not_1_out));  // open: preset
  J_K_Flip_Flop j_k_ff_3 (
    .J(Cp), .K(Cp), .clk(j_k_ff_2_qn), .Q(j_k_ff_1_q[2]), .Qn(j_k_ff_3_qn), .reset(not_1_out));  // open: preset
  assign Saida = Ep ? j_k_ff_1_q : 4'bz;  // Controlled_Buffer controlled_buffer_1
  J_K_Flip_Flop j_k_ff_4 (.J(Cp), .K(Cp), .clk(j_k_ff_3_qn), .Q(j_k_ff_1_q[3]), .reset(not_1_out));  // open: Qn, preset
endmodule

module AC (
  input  [7:0] Do_Barramento,
  input  La,
  input  CLK,
  input  Ea,
  output [7:0] Para_Barramento,
  output [7:0] Para_Add_Sub
);

  wire not_1_out;
  wire [7:0] controlled_buffer_1_out;

  assign controlled_buffer_1_out = not_1_out ? Do_Barramento : 8'bz;  // Controlled_Buffer controlled_buffer_1
  not not_1 (not_1_out, La);
  D_Flip_Flop d_ff_1 (.D(controlled_buffer_1_out[7]), .clk(CLK), .Q(Para_Add_Sub[7]));  // open: Qn, preset, reset
  D_Flip_Flop d_ff_2 (.D(controlled_buffer_1_out[6]), .clk(CLK), .Q(Para_Add_Sub[6]));  // open: Qn, preset, reset
  D_Flip_Flop d_ff_3 (.D(controlled_buffer_1_out[5]), .clk(CLK), .Q(Para_Add_Sub[5]));  // open: Qn, preset, reset
  assign Para_Barramento = Ea ? Para_Add_Sub : 8'bz;  // Controlled_Buffer controlled_buffer_2
  D_Flip_Flop d_ff_4 (.D(controlled_buffer_1_out[4]), .clk(CLK), .Q(Para_Add_Sub[4]));  // open: Qn, preset, reset
  D_Flip_Flop d_ff_5 (.D(controlled_buffer_1_out[3]), .clk(CLK), .Q(Para_Add_Sub[3]));  // open: Qn, preset, reset
  D_Flip_Flop d_ff_6 (.D(controlled_buffer_1_out[2]), .clk(CLK), .Q(Para_Add_Sub[2]));  // open: Qn, preset, reset
  D_Flip_Flop d_ff_7 (.D(controlled_buffer_1_out[1]), .clk(CLK), .Q(Para_Add_Sub[1]));  // open: Qn, preset, reset
  D_Flip_Flop d_ff_8 (.D(controlled_buffer_1_out[0]), .clk(CLK), .Q(Para_Add_Sub[0]));  // open: Qn, preset, reset
endmodule

module SomadorCompleto (
  input  A,
  input  B,
  input  Cin,
  output Soma,
  output Vai1
);

  wire and_1_out, and_2_out, xor_1_out;

  xor xor_1 (xor_1_out, A, B);
  and and_1 (and_1_out, A, B);
  xor xor_2 (Soma, xor_1_out, Cin);
  and and_2 (and_2_out, xor_1_out, Cin);
  or or_1 (Vai1, and_2_out, and_1_out);
endmodule

module RB (
  input  [7:0] Do_Barramento,
  input  Lb,
  input  CLK,
  output [7:0] Para_Add_Sub
);

  wire not_1_out;
  wire [7:0] controlled_buffer_1_out;

  assign controlled_buffer_1_out = not_1_out ? Do_Barramento : 8'bz;  // Controlled_Buffer controlled_buffer_1
  not not_1 (not_1_out, Lb);
  D_Flip_Flop d_ff_1 (.D(controlled_buffer_1_out[7]), .clk(CLK), .Q(Para_Add_Sub[7]));  // open: Qn, preset, reset
  D_Flip_Flop d_ff_2 (.D(controlled_buffer_1_out[6]), .clk(CLK), .Q(Para_Add_Sub[6]));  // open: Qn, preset, reset
  D_Flip_Flop d_ff_3 (.D(controlled_buffer_1_out[5]), .clk(CLK), .Q(Para_Add_Sub[5]));  // open: Qn, preset, reset
  D_Flip_Flop d_ff_4 (.D(controlled_buffer_1_out[4]), .clk(CLK), .Q(Para_Add_Sub[4]));  // open: Qn, preset, reset
  D_Flip_Flop d_ff_5 (.D(controlled_buffer_1_out[3]), .clk(CLK), .Q(Para_Add_Sub[3]));  // open: Qn, preset, reset
  D_Flip_Flop d_ff_6 (.D(controlled_buffer_1_out[2]), .clk(CLK), .Q(Para_Add_Sub[2]));  // open: Qn, preset, reset
  D_Flip_Flop d_ff_7 (.D(controlled_buffer_1_out[1]), .clk(CLK), .Q(Para_Add_Sub[1]));  // open: Qn, preset, reset
  D_Flip_Flop d_ff_8 (.D(controlled_buffer_1_out[0]), .clk(CLK), .Q(Para_Add_Sub[0]));  // open: Qn, preset, reset
endmodule

module RS (
  input  [7:0] Do_Barramento,
  input  La,
  input  CLK,
  input  CLR,
  output [7:0] Para_Display
);

  wire not_1_out;
  wire [7:0] controlled_buffer_1_out;

  assign controlled_buffer_1_out = not_1_out ? Do_Barramento : 8'bz;  // Controlled_Buffer controlled_buffer_1
  not not_1 (not_1_out, La);
  D_Flip_Flop d_ff_1 (.D(controlled_buffer_1_out[7]), .clk(CLK), .Q(Para_Display[7]), .reset(CLR));  // open: Qn, preset
  D_Flip_Flop d_ff_2 (.D(controlled_buffer_1_out[6]), .clk(CLK), .Q(Para_Display[6]), .reset(CLR));  // open: Qn, preset
  D_Flip_Flop d_ff_3 (.D(controlled_buffer_1_out[5]), .clk(CLK), .Q(Para_Display[5]), .reset(CLR));  // open: Qn, preset
  D_Flip_Flop d_ff_4 (.D(controlled_buffer_1_out[4]), .clk(CLK), .Q(Para_Display[4]), .reset(CLR));  // open: Qn, preset
  D_Flip_Flop d_ff_5 (.D(controlled_buffer_1_out[3]), .clk(CLK), .Q(Para_Display[3]), .reset(CLR));  // open: Qn, preset
  D_Flip_Flop d_ff_6 (.D(controlled_buffer_1_out[2]), .clk(CLK), .Q(Para_Display[2]), .reset(CLR));  // open: Qn, preset
  D_Flip_Flop d_ff_7 (.D(controlled_buffer_1_out[1]), .clk(CLK), .Q(Para_Display[1]), .reset(CLR));  // open: Qn, preset
  D_Flip_Flop d_ff_8 (.D(controlled_buffer_1_out[0]), .clk(CLK), .Q(Para_Display[0]), .reset(CLR));  // open: Qn, preset
endmodule

// MAR
module REM4bits (
  input  CLK,
  input  [3:0] in_2,
  input  Lm,
  output [3:0] out_4
);

  wire not_1_out;
  wire [3:0] controlled_buffer_1_out;

  D_Flip_Flop d_ff_1 (.D(controlled_buffer_1_out[3]), .clk(CLK), .Q(out_4[3]));  // open: Qn, preset, reset
  D_Flip_Flop d_ff_2 (.D(controlled_buffer_1_out[2]), .clk(CLK), .Q(out_4[2]));  // open: Qn, preset, reset
  not not_1 (not_1_out, Lm);
  assign controlled_buffer_1_out = not_1_out ? in_2 : 4'bz;  // Controlled_Buffer controlled_buffer_1
  D_Flip_Flop d_ff_3 (.D(controlled_buffer_1_out[1]), .clk(CLK), .Q(out_4[1]));  // open: Qn, preset, reset
  D_Flip_Flop d_ff_4 (.D(controlled_buffer_1_out[0]), .clk(CLK), .Q(out_4[0]));  // open: Qn, preset, reset
endmodule

// Complemento1
module Complemento_1 (
  input  A7,
  input  A6,
  input  A5,
  input  A4,
  input  A3,
  input  A2,
  input  A1,
  input  A0,
  input  in_9,
  output R7,
  output R6,
  output R5,
  output R4,
  output R3,
  output R2,
  output R1,
  output R0
);

  xor xor_1 (R7, A7, in_9);
  xor xor_2 (R6, A6, in_9);
  xor xor_3 (R5, A5, in_9);
  xor xor_4 (R4, A4, in_9);
  xor xor_5 (R3, A3, in_9);
  xor xor_6 (R2, A2, in_9);
  xor xor_7 (R1, A1, in_9);
  xor xor_8 (R0, A0, in_9);
endmodule

// Complemento2
module Complemento_2 (
  input  A0,
  input  A1,
  input  A2,
  input  A3,
  input  A4,
  input  A5,
  input  A6,
  input  A7,
  input  in_9,
  output out_10,
  output out_11,
  output out_12,
  output out_13,
  output out_14,
  output out_15,
  output out_16,
  output out_17
);

  wire meiosomador_1_vai1, meiosomador_2_vai1, meiosomador_3_vai1, meiosomador_4_vai1, meiosomador_5_vai1,
       meiosomador_6_vai1, meiosomador_7_vai1;

  MeioSomador meiosomador_1 (.A(A0), .VEM1(in_9), .Soma(out_10), .VAI1(meiosomador_1_vai1));
  MeioSomador meiosomador_2 (.A(A1), .VEM1(meiosomador_1_vai1), .Soma(out_11), .VAI1(meiosomador_2_vai1));
  MeioSomador meiosomador_3 (.A(A2), .VEM1(meiosomador_2_vai1), .Soma(out_12), .VAI1(meiosomador_3_vai1));
  MeioSomador meiosomador_4 (.A(A3), .VEM1(meiosomador_3_vai1), .Soma(out_13), .VAI1(meiosomador_4_vai1));
  MeioSomador meiosomador_5 (.A(A4), .VEM1(meiosomador_4_vai1), .Soma(out_14), .VAI1(meiosomador_5_vai1));
  MeioSomador meiosomador_6 (.A(A5), .VEM1(meiosomador_5_vai1), .Soma(out_15), .VAI1(meiosomador_6_vai1));
  MeioSomador meiosomador_7 (.A(A6), .VEM1(meiosomador_6_vai1), .Soma(out_16), .VAI1(meiosomador_7_vai1));
  MeioSomador meiosomador_8 (.A(A7), .VEM1(meiosomador_7_vai1), .Soma(out_17));  // open: VAI1
endmodule

// SUM/SUB
module Somador_Subtrator (
  input  [7:0] B,
  input  Su,
  input  [7:0] A,
  input  Eu,
  output [7:0] out_5
);

  wire complemento_1_1_r0, complemento_1_1_r1, complemento_1_1_r2, complemento_1_1_r3, complemento_1_1_r4,
       complemento_1_1_r5, complemento_1_1_r6, complemento_1_1_r7, complemento_2_1_out_10,
       complemento_2_1_out_11, complemento_2_1_out_12, complemento_2_1_out_13, complemento_2_1_out_14,
       complemento_2_1_out_15, complemento_2_1_out_16, complemento_2_1_out_17, somador_4bits_1_out_11,
       somador_4bits_1_out_13, somador_4bits_1_out_14, somador_4bits_1_resultado, somador_4bits_1_vai1,
       somador_4bits_2_out_11, somador_4bits_2_out_13, somador_4bits_2_out_14, somador_4bits_2_resultado,
       somador_4bits_2_vai1;

  LED led_1 (.in(somador_4bits_1_vai1));
  Somador_4Bits somador_4bits_1 (
    .Vai1(somador_4bits_1_vai1), .in_1(A[7]), .A(A[6]), .in_3(A[5]), .in_4(A[4]),
    .in_5(complemento_2_1_out_17), .B(complemento_2_1_out_16), .in_7(complemento_2_1_out_15),
    .in_8(complemento_2_1_out_14), .Vem1(somador_4bits_2_vai1), .out_11(somador_4bits_1_out_11),
    .Resultado(somador_4bits_1_resultado), .out_13(somador_4bits_1_out_13), .out_14(somador_4bits_1_out_14));
  assign out_5[5] = Eu ? somador_4bits_1_out_13 : 1'bz;  // Controlled_Buffer controlled_buffer_1
  assign out_5[6] = Eu ? somador_4bits_1_resultado : 1'bz;  // Controlled_Buffer controlled_buffer_2
  assign out_5[7] = Eu ? somador_4bits_1_out_11 : 1'bz;  // Controlled_Buffer controlled_buffer_3
  Somador_4Bits somador_4bits_2 (
    .Vai1(somador_4bits_2_vai1), .in_1(A[3]), .A(A[2]), .in_3(A[1]), .in_4(A[0]),
    .in_5(complemento_2_1_out_13), .B(complemento_2_1_out_12), .in_7(complemento_2_1_out_11),
    .in_8(complemento_2_1_out_10), .Vem1(1'b0), .out_11(somador_4bits_2_out_11),
    .Resultado(somador_4bits_2_resultado), .out_13(somador_4bits_2_out_13), .out_14(somador_4bits_2_out_14));
  assign out_5[1] = Eu ? somador_4bits_2_out_13 : 1'bz;  // Controlled_Buffer controlled_buffer_4
  assign out_5[2] = Eu ? somador_4bits_2_resultado : 1'bz;  // Controlled_Buffer controlled_buffer_5
  assign out_5[3] = Eu ? somador_4bits_2_out_11 : 1'bz;  // Controlled_Buffer controlled_buffer_6
  assign out_5[4] = Eu ? somador_4bits_1_out_14 : 1'bz;  // Controlled_Buffer controlled_buffer_7
  Complemento_2 complemento_2_1 (
    .in_9(Su), .A0(complemento_1_1_r0), .A1(complemento_1_1_r1), .A2(complemento_1_1_r2),
    .A3(complemento_1_1_r3), .A4(complemento_1_1_r4), .A5(complemento_1_1_r5), .A6(complemento_1_1_r6),
    .A7(complemento_1_1_r7), .out_10(complemento_2_1_out_10), .out_11(complemento_2_1_out_11),
    .out_12(complemento_2_1_out_12), .out_13(complemento_2_1_out_13), .out_14(complemento_2_1_out_14),
    .out_15(complemento_2_1_out_15), .out_16(complemento_2_1_out_16), .out_17(complemento_2_1_out_17));
  assign out_5[0] = Eu ? somador_4bits_2_out_14 : 1'bz;  // Controlled_Buffer controlled_buffer_8
  Complemento_1 complemento_1_1 (
    .A7(B[7]), .A6(B[6]), .A5(B[5]), .A4(B[4]), .A3(B[3]), .A2(B[2]), .A1(B[1]), .A0(B[0]),
    .R7(complemento_1_1_r7), .R6(complemento_1_1_r6), .R5(complemento_1_1_r5), .R4(complemento_1_1_r4),
    .R3(complemento_1_1_r3), .R2(complemento_1_1_r2), .R1(complemento_1_1_r1), .R0(complemento_1_1_r0),
    .in_9(Su));
endmodule

// somador 4b
module Somador_4Bits (
  input  in_1,
  input  A,
  input  in_3,
  input  in_4,
  input  in_5,
  input  B,
  input  in_7,
  input  in_8,
  input  Vem1,
  output Vai1,
  output out_11,
  output Resultado,
  output out_13,
  output out_14
);

  wire somadorcompleto_2_vai1, somadorcompleto_3_vai1, somadorcompleto_4_vai1;

  SomadorCompleto somadorcompleto_1 (.A(in_1), .B(in_5), .Cin(somadorcompleto_2_vai1), .Soma(out_11), .Vai1(Vai1));
  SomadorCompleto somadorcompleto_2 (
    .A(A), .B(B), .Cin(somadorcompleto_3_vai1), .Soma(Resultado), .Vai1(somadorcompleto_2_vai1));
  SomadorCompleto somadorcompleto_3 (
    .A(in_3), .B(in_7), .Cin(somadorcompleto_4_vai1), .Soma(out_13), .Vai1(somadorcompleto_3_vai1));
  SomadorCompleto somadorcompleto_4 (.A(in_4), .B(in_8), .Cin(Vem1), .Soma(out_14), .Vai1(somadorcompleto_4_vai1));
endmodule

module Controlador (
  input  CLR_CPU,
  input  CLK_CPU,
  input  X7,
  input  X6,
  input  X5,
  input  X4,
  output NOT_CLR,
  output CLR,
  output CLK,
  output NOT_CLK,
  output [5:0] Timer,
  output Cp,
  output Ep,
  output NOT_Lm,
  output NOT_CE,
  output NOT_L1,
  output NOT_E1,
  output NOT_La,
  output Ea,
  output Su,
  output Eu,
  output NOT_Lb,
  output NOT_Lo
);

  wire ADD, HLT, j_k_ff_1_q, j_k_ff_2_qn, j_k_ff_3_qn, j_k_ff_4_qn, j_k_ff_5_qn, j_k_ff_6_qn, LDA,
       nand_1_out, nand_2_out, nand_3_out, nand_4_out, nand_5_out, nand_6_out, nand_7_out, nand_8_out,
       nand_9_out, nand_10_out, nand_11_out, nand_12_out, nand_13_out, nand_14_out, nand_15_out, nand_16_out,
       nand_17_out, nand_18_out, not_1_out, not_2_out, not_3_out, not_4_out, not_6_out, not_8_out, not_9_out,
       not_10_out, not_12_out, not_13_out, not_14_out, not_15_out, not_16_out, not_17_out, not_18_out,
       not_21_out, not_22_out, not_24_out, not_25_out, not_26_out, not_27_out, not_31_out, not_32_out,
       not_33_out, not_34_out, or_1_out, or_2_out, or_3_out, or_4_out, or_6_out, OUT, SUB;

  not not_1 (not_1_out, X7);
  not not_2 (not_2_out, HLT);
  not not_3 (not_3_out, X6);
  and and_1 (CLK, not_2_out, CLK_CPU);
  not not_4 (not_4_out, X5);
  not not_5 (NOT_CLR, CLR_CPU);
  not not_6 (not_6_out, X4);
  not not_7 (NOT_CLK, CLK);
  J_K_Flip_Flop j_k_ff_1 (
    .J(j_k_ff_6_qn), .clk(CLK), .K(Timer[5]), .Q(j_k_ff_1_q), .Qn(Ep), .reset(CLR_CPU));  // open: preset
  and and_2 (LDA, not_1_out, not_3_out, not_4_out, not_6_out);
  and and_3 (ADD, not_1_out, not_3_out, not_4_out, X4);
  and and_4 (SUB, not_1_out, not_3_out, X5, not_6_out);
  and and_5 (OUT, X7, X6, X5, not_6_out);
  and and_6 (HLT, X7, X6, X5, X4);
  J_K_Flip_Flop j_k_ff_2 (
    .J(Ep), .clk(CLK), .K(j_k_ff_1_q), .Q(Cp), .Qn(j_k_ff_2_qn), .reset(CLR_CPU));  // open: preset
  J_K_Flip_Flop j_k_ff_3 (
    .J(Cp), .clk(CLK), .K(j_k_ff_2_qn), .Q(Timer[2]), .Qn(j_k_ff_3_qn), .reset(CLR_CPU));  // open: preset
  J_K_Flip_Flop j_k_ff_4 (
    .J(Timer[2]), .clk(CLK), .K(j_k_ff_3_qn), .Q(Timer[3]), .Qn(j_k_ff_4_qn), .reset(CLR_CPU));  // open: preset
  not not_8 (not_8_out, Ep);
  J_K_Flip_Flop j_k_ff_5 (
    .J(Timer[3]), .clk(CLK), .K(j_k_ff_4_qn), .Q(Timer[4]), .Qn(j_k_ff_5_qn), .reset(CLR_CPU));  // open: preset
  nand nand_1 (nand_1_out, LDA, Timer[3]);
  nand nand_2 (nand_2_out, ADD, Timer[3]);
  not not_9 (not_9_out, not_8_out);
  not not_10 (not_10_out, nand_1_out);
  or or_1 (or_1_out, not_9_out, not_10_out, not_12_out, not_13_out);
  not not_11 (NOT_Lm, or_1_out);
  nand nand_3 (nand_3_out, SUB, Timer[3]);
  not not_12 (not_12_out, nand_2_out);
  not not_13 (not_13_out, nand_3_out);
  J_K_Flip_Flop j_k_ff_6 (
    .J(Timer[4]), .clk(CLK), .K(j_k_ff_5_qn), .Q(Timer[5]), .Qn(j_k_ff_6_qn), .reset(CLR_CPU));  // open: preset
  not not_14 (not_14_out, Timer[2]);
  nand nand_4 (nand_4_out, LDA, Timer[4]);
  not not_15 (not_15_out, not_14_out);
  nand nand_5 (nand_5_out, ADD, Timer[4]);
  not not_16 (not_16_out, nand_4_out);
  not not_17 (not_17_out, nand_5_out);
  not not_18 (not_18_out, nand_6_out);
  or or_2 (or_2_out, not_15_out, not_16_out, not_17_out, not_18_out);
  not not_19 (NOT_CE, or_2_out);
  nand nand_6 (nand_6_out, SUB, Timer[4]);
  nand nand_7 (nand_7_out, LDA, Timer[3]);
  not not_20 (NOT_L1, Timer[2]);
  nand nand_8 (nand_8_out, ADD, Timer[3]);
  not not_21 (not_21_out, nand_7_out);
  not not_22 (not_22_out, nand_8_out);
  or or_3 (or_3_out, not_21_out, not_22_out, not_24_out);
  not not_23 (NOT_E1, or_3_out);
  nand nand_9 (nand_9_out, SUB, Timer[3]);
  not not_24 (not_24_out, nand_9_out);
  nand nand_10 (nand_10_out, LDA, Timer[4]);
  nand nand_11 (nand_11_out, ADD, Timer[5]);
  not not_25 (not_25_out, nand_10_out);
  not not_26 (not_26_out, nand_11_out);
  not not_27 (not_27_out, nand_12_out);
  or or_4 (or_4_out, not_25_out, not_26_out, not_27_out);
  not not_28 (NOT_La, or_4_out);
  nand nand_12 (nand_12_out, SUB, Timer[5]);
  nand nand_13 (nand_13_out, OUT, Timer[3]);
  not not_29 (Ea, nand_13_out);
  nand nand_14 (nand_14_out, SUB, Timer[5]);
  not not_30 (Su, nand_14_out);
  nand nand_15 (nand_15_out, ADD, Timer[5]);
  nand nand_16 (nand_16_out, SUB, Timer[5]);
  not not_31 (not_31_out, nand_15_out);
  not not_32 (not_32_out, nand_16_out);
  or or_5 (Eu, not_31_out, not_32_out);
  nand nand_17 (nand_17_out, ADD, Timer[4]);
  not not_33 (not_33_out, nand_17_out);
  not not_34 (not_34_out, nand_18_out);
  or or_6 (or_6_out, not_33_out, not_34_out);
  not not_35 (NOT_Lb, or_6_out);
  nand nand_18 (nand_18_out, SUB, Timer[4]);
  nand nand_19 (NOT_Lo, Timer[3], OUT);

  assign CLR = CLR_CPU;
  assign Timer[1:0] = {Cp, Ep};

  // Other names for the same wires on the sheet: T1 = Ep; T2 = Cp; T3 = Timer[2]; T4 = Timer[3]; T5 = Timer[4];
  //   T6 = Timer[5]
endmodule

module RI (
  input  Ei,
  input  CLK,
  input  CLR,
  input  [7:0] In,
  input  Li,
  output [3:0] Out,
  output X7,
  output X6,
  output X5,
  output X4
);

  wire d_ff_5_q, d_ff_6_q, d_ff_7_q, d_ff_8_q, not_1_out, not_2_out;
  wire [7:0] controlled_buffer_3_out;

  not not_1 (not_1_out, Ei);
  D_Flip_Flop d_ff_1 (.clk(CLK), .D(controlled_buffer_3_out[7]), .Q(X7), .reset(CLR));  // open: Qn, preset
  D_Flip_Flop d_ff_2 (.clk(CLK), .D(controlled_buffer_3_out[6]), .Q(X6), .reset(CLR));  // open: Qn, preset
  D_Flip_Flop d_ff_3 (.clk(CLK), .D(controlled_buffer_3_out[5]), .Q(X5), .reset(CLR));  // open: Qn, preset
  D_Flip_Flop d_ff_4 (.clk(CLK), .D(controlled_buffer_3_out[4]), .Q(X4), .reset(CLR));  // open: Qn, preset
  assign Out[3] = not_1_out ? d_ff_5_q : 1'bz;  // Controlled_Buffer controlled_buffer_1
  D_Flip_Flop d_ff_5 (.clk(CLK), .D(controlled_buffer_3_out[3]), .Q(d_ff_5_q), .reset(CLR));  // open: Qn, preset
  not not_2 (not_2_out, Li);
  assign Out[2] = not_1_out ? d_ff_6_q : 1'bz;  // Controlled_Buffer controlled_buffer_2
  D_Flip_Flop d_ff_6 (.clk(CLK), .D(controlled_buffer_3_out[2]), .Q(d_ff_6_q), .reset(CLR));  // open: Qn, preset
  assign controlled_buffer_3_out = not_2_out ? In : 8'bz;  // Controlled_Buffer controlled_buffer_3
  assign Out[1] = not_1_out ? d_ff_7_q : 1'bz;  // Controlled_Buffer controlled_buffer_4
  D_Flip_Flop d_ff_7 (.clk(CLK), .D(controlled_buffer_3_out[1]), .Q(d_ff_7_q), .reset(CLR));  // open: Qn, preset
  assign Out[0] = not_1_out ? d_ff_8_q : 1'bz;  // Controlled_Buffer controlled_buffer_5
  D_Flip_Flop d_ff_8 (.clk(CLK), .D(controlled_buffer_3_out[0]), .Q(d_ff_8_q), .reset(CLR));  // open: Qn, preset
endmodule
